# Fritzing sketch MQ135_DHT22_GPY (saved by Fritzing 0.9.2b)
breadboards: 1

parts:
  Parte1 = Arduino Uno (Rev3)
  Sensor1 = Gas Sensor Breakout Board
  DHT1 = DHT22 Humidity and Temperature Sensor
  U1 = Sharp Dust Sensor [part_number=GP2Y1010AU0F]
  R1 = Resistor [tolerance=±5% resistance=150 package="1206 [SMD]"]
  C1 = Electrolytic Capacitor [capacitance=100µF package="200 mil [THT, electrolytic]"]

nets:
  N1: Parte1.A0, Sensor1.GND
  N2: Parte1.A1, U1.Vo
  N3: Parte1.D3_PWM, U1.LED
  N4: Parte1.D4, DHT1.DATA
  5V: Parte1.5V, Sensor1.5V, DHT1.VDD, U1.VCC, R1.Pin_0
  GND: Parte1.GND, Sensor1.DOUT, DHT1.GND, U1.LED-GND, U1.S-GND, C1.-
  N5: U1.V-LED, R1.Pin_1

custom parts:
  Gas Sensor Breakout Board: Gas sensor breakout board. Input voltage is 5V. Sensor output is available in analog and digital.
  Sharp Dust Sensor: Sharp GP2Y1010AU0F Dust Sensor
