# Fritzing sketch MQ7_DHT11_BMP180 (saved by Fritzing 0.9.2b)
breadboards: 1

parts:
  Parte1 = Arduino Uno (Rev3)
  DHT1 = DHT11 Humitidy and Temperature Sensor
  Parte2 = MQ-7 breakout
  Parte3 = BMP180 Breakout (GY-68)

nets:
  N1: Parte1.A0, Parte2.AO
  N2: Parte1.A4/SDA, Parte3.SDA
  N3: Parte1.A5/SCL, Parte3.SCL
  N4: Parte1.D2, DHT1.DATA
  VCC: Parte1.5V, DHT1.VDD, Parte2.VCC, Parte3.VCC
  GND: Parte1.GND, DHT1.GND, Parte2.GND, Parte3.GND

custom parts:
  DHT11 Humitidy and Temperature Sensor: DHT11 Humidity and Temperature Sensor
  MQ-7 breakout: SKU: 101282
  BMP180 Breakout (GY-68): This is a simple breakout board for the BMP180, a high-precision, low-power barometric pressure sensor made by Bosch Sensortec. The range of measurement is from 300hPa to 1100hPa. The sensor can be supplied with voltage ranging from 1.8V to 3.6V. Operating temperature range is -40 to +85 °C. This particular breakout board (or perhaps the configuration) is produced by Shenzhen Keep Power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
